# Fritzing sketch esp8266-wemos-d1-mini-and-bme280-i2c-0x76 (saved by Fritzing 0.9.2b)
breadboards: 1

parts:
  WeMos_D1_Mini1 = WeMos D1 Mini
  Part1 = Adafruit BME280

nets:
  3V3: WeMos_D1_Mini1.3V3, Part1.3.3V
  N1: WeMos_D1_Mini1.D1, Part1.SCK/SCL
  N2: WeMos_D1_Mini1.D2, Part1.SDI/SDA
  N3: WeMos_D1_Mini1.G, Part1.GND

custom parts:
  Adafruit BME280: Bosch has stepped up their game with their new BME280 sensor, an environmental sensor with temperature, barometric pressure and humidity! This sensor is great for all sorts of weather/environmental sensing and can even be used in both I2C and SPI! This precision sensor from Bosch is the best low-cost sensing solution for measuring humidity with ±3% accuracy, barometric pressure with ±1 hPa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
