# Fritzing sketch esp8266-wemos-d1-mini-and-oled-and-bme280-spi (saved by Fritzing 0.9.2b)
breadboards: 1

parts:
  WeMos_D1_Mini1 = WeMos D1 Mini
  Part2 = Adafruit BME280
  Squix1 = OLED 0.96" 128x64 I2C SSD1306

nets:
  3V3: WeMos_D1_Mini1.3V3, Part2.3.3V, Squix1.VCC
  N1: WeMos_D1_Mini1.D1, Squix1.SCL
  N2: WeMos_D1_Mini1.D2, Squix1.SCA
  N3: WeMos_D1_Mini1.D5, Part2.SCK/SCL
  N4: WeMos_D1_Mini1.D6, Part2.SDO/ADR
  N5: WeMos_D1_Mini1.D7, Part2.SDI/SDA
  N6: WeMos_D1_Mini1.D8, Part2.CS
  GND: WeMos_D1_Mini1.G, Part2.GND, Squix1.GND

custom parts:
  Adafruit BME280: Bosch has stepped up their game with their new BME280 sensor, an environmental sensor with temperature, barometric pressure and humidity! This sensor is great for all sorts of weather/environmental sensing and can even be used in both I2C and SPI! This precision sensor from Bosch is the best low-cost sensing solution for measuring humidity with ±3% accuracy, barometric pressure with ±1 hPa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
